# Fritzing sketch breadboard (saved by Fritzing 0.9.3b)
breadboards: 1

parts:
  Part1 = Adafruit VS1053 Codec + MicroSD Breakout - MP3/WAV/MIDI/OGG [part_number="Adafruit #1381"]
  Teensy_3_1 = Teensy 3.1  # not connected
  Part2 = OLED Monochrome 128x64 0.96 inch [part_number=326]
  ENCODER1 = Rotary Encoder with Knob
  TRS1 = Audio Jack (TRS) 3.5mm [package="4Ucon 08780 [THT]"]
  J1 = Piezo Speaker

nets:
  N1: Part1.R_OUT, TRS1.Ring
  N2: Part1.L_OUT, TRS1.Tip
  N3: Part1.AGND, TRS1.Sleeve
  GND: Part1.GND, Part2.GND, ENCODER1.no_name_yet#2, ENCODER1.no_name_yet#4, J1.pin1
  3.3V: Part1.3.3V, Part2.VIN
  N4: Part1.MISO, Part2.DC_SA0
  N5: Part1.MOSI_5V, Part2.MOSI_SDA
  N6: Part1.SCLK_5V, Part2.SCLK_SCK

custom parts:
  Adafruit VS1053 Codec + MicroSD Breakout - MP3/WAV/MIDI/OGG: This breakout board is the ultimate companion for the VLSI VS1053B DSP codec chip. The VS1053 can decode a wide variety of audio formats such as MP3, AAC, Ogg Vorbis, WMA, MIDI, FLAC, WAV (PCM and ADPCM). It can also be used to record audio in both PCM (WAV) and compressed Ogg Vorbis. You can do all sorts of stuff with the audio as well such as adjusting bass, treble, and volume digitally.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
  OLED Monochrome 128x64 0.96 inch: These displays are small, only about 1" diameter, but very readable due to the high contrast of an OLED display. This display is made of 128x64 individual white OLED pixels, each one is turned on or off by the controller chip. Because the display makes its own light, no backlight is required. This reduces the power required to run the OLED and is why the display has such high contrast; we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
  Rotary Encoder with Knob: Rotary Encoder with 1/4" Shaft and Knob
